// Logisim project 7bitadder.circ as structural Verilog: 1 circuit, main circuit main
module main (
  input  in_1,
  input  in_2,
  input  in_3,
  input  in_4,
  input  in_5,
  input  in_6,
  input  in_7,
  input  in_8,
  input  in_9,
  input  in_10,
  input  in_11,
  input  in_12,
  input  in_13,
  input  in_14,
  input  in_15,
  output out_16,
  output out_17,
  output out_18,
  output out_19,
  output out_20,
  output out_21,
  output out_22,
  output out_23
);

  wire main_2_carry, main_3_carry, main_4_carry, main_5_carry, main_6_carry, main_7_carry;

  fulladder_main main_1 (.A(in_3), .B(in_2), .Cin(main_2_carry), .Sum(out_17), .Carry(out_16));
  fulladder_main main_2 (.A(in_5), .B(in_4), .Cin(main_3_carry), .Sum(out_18), .Carry(main_2_carry));
  fulladder_main main_3 (.A(in_7), .B(in_6), .Cin(main_4_carry), .Sum(out_19), .Carry(main_3_carry));
  fulladder_main main_4 (.A(in_9), .B(in_8), .Cin(main_5_carry), .Sum(out_20), .Carry(main_4_carry));
  fulladder_main main_5 (.A(in_11), .B(in_10), .Cin(main_6_carry), .Sum(out_21), .Carry(main_5_carry));
  fulladder_main main_6 (.A(in_13), .B(in_12), .Cin(main_7_carry), .Sum(out_22), .Carry(main_6_carry));
  fulladder_main main_7 (.A(in_15), .B(in_14), .Cin(in_1), .Sum(out_23), .Carry(main_7_carry));

  // Notes on the sheet:
  //   7 BIT BINARY RIPPLE ADDER
endmodule
