// Logisim project Logisim-121-202.circ as structural Verilog: 1 circuit, main circuit main
module main (
  input  _1,
  input  _2,
  input  _3,
  input  _4,
  input  _5,
  input  _6,
  input  _7,
  input  _8,
  input  _9,
  input  _10,
  input  _11,
  input  _12,
  input  _13,
  input  _14,
  input  _15,
  input  _16,
  input  _17,
  input  _18,
  input  _19,
  input  _20,
  input  _21,
  input  _22,
  input  _23,
  input  _24,
  input  _25,
  input  _26,
  input  Caps,
  input  Lock
);

  wire a_out, and_1_out, and_2_out, b_out, button_1_out, c_out, d_out, e_out, f_out, g_out, h_out, i_out,
       j_out, k_out, l_out, m_out, main_1_out_27, main_1_out_28, main_1_out_29, main_1_out_30, main_1_out_31,
       main_2_out_12, main_2_out_13, main_2_out_16, main_2_s0, main_2_s2, main_2_s3, main_3_out_27,
       main_3_out_28, main_3_out_29, main_3_out_30, main_3_out_31, main_4_out_14, main_4_out_17, main_4_s0,
       main_4_s2, main_4_s3, main_4_s5, main_4_s6, main_5_out_13, main_5_out_16, main_5_s0, main_5_s2,
       main_5_s3, n_out, not_1_out, not_2_out, not_3_out, o_out, or_1_out, or_2_out, p_out, q_out, r_out,
       s_out, t_out, u_out, v_out, w_out, x_out, xor_1_out, xor_2_out, xor_3_out, xor_4_out, xor_5_out,
       xor_6_out, xor_7_out, xor_8_out, y_out, z_out;
  wire [6:0] main_6_out_23;

  alpha_to_bin_main main_1 (
    .a(a_out), .b(b_out), .c(c_out), .d(d_out), .e(e_out), .f(f_out), .g(g_out), .h(h_out), .i(i_out),
    .j(j_out), .k(k_out), .l(l_out), .m(m_out), .n(n_out), .o(o_out), .p(p_out), .q(q_out), .r(r_out),
    .s(s_out), .t(t_out), .u(u_out), .v(v_out), .w(w_out), .x(x_out), .y(y_out), .z(z_out),
    .out_27(main_1_out_27), .out_28(main_1_out_28), .out_29(main_1_out_29), .out_30(main_1_out_30),
    .out_31(main_1_out_31));
  Button a (.out(a_out));
  Button b (.out(b_out));
  not not_1 (not_1_out, Caps);
  Button c (.out(c_out));
  Button d (.out(d_out));
  xor xor_1 (xor_1_out, Lock, main_3_out_27);
  _5bitadder_main main_2 (
    .B4(xor_1_out), .A4(main_1_out_27), .B3(xor_2_out), .A3(main_1_out_28), .B2(xor_3_out),
    .A2(main_1_out_29), .B1(xor_5_out), .A1(main_1_out_30), .B0(Lock), .in_10(xor_4_out), .A0(main_1_out_31),
    .out_12(main_2_out_12), .out_13(main_2_out_13), .S3(main_2_s3), .S2(main_2_s2), .out_16(main_2_out_16),
    .S0(main_2_s0));
  xor xor_2 (xor_2_out, Lock, main_3_out_28);
  xor xor_3 (xor_3_out, Lock, main_3_out_29);
  xor xor_4 (xor_4_out, Lock, main_3_out_31);
  Button e (.out(e_out));
  xor xor_5 (xor_5_out, main_3_out_30, Lock);
  Button f (.out(f_out));
  Button g (.out(g_out));
  or or_1 (or_1_out, a_out, b_out, c_out, d_out, e_out, f_out, g_out, h_out, i_out, j_out, k_out, l_out, m_out, n_out, o_out, p_out, q_out, r_out, s_out, t_out, u_out, v_out, w_out, x_out, y_out, z_out);
  shift_to_bin_main main_3 (
    ._1(_1), ._2(_2), ._3(_3), ._4(_4), ._5(_5), ._6(_6), ._7(_7), ._8(_8), ._9(_9), ._10(_10), ._11(_11),
    ._12(_12), ._13(_13), ._14(_14), ._15(_15), ._16(_16), ._17(_17), ._18(_18), ._19(_19), ._20(_20),
    ._21(_21), ._22(_24), ._23(_22), ._24(_23), ._25(_25), ._26(_26), .out_27(main_3_out_27),
    .out_28(main_3_out_28), .out_29(main_3_out_29), .out_30(main_3_out_30), .out_31(main_3_out_31));
  Button h (.out(h_out));
  and and_1 (and_1_out, not_2_out, main_2_s2, main_2_s3, main_2_out_13);
  and and_2 (and_2_out, main_2_out_13, main_2_s3, main_2_out_16, not_2_out);
  not not_2 (not_2_out, Lock);
  Button j (.out(j_out));
  Button i (.out(i_out));
  not not_3 (not_3_out, or_1_out);
  xor xor_6 (xor_6_out, main_2_out_12, Lock);
  Button l (.out(l_out));
  Button k (.out(k_out));
  or or_2 (or_2_out, and_1_out, and_2_out, xor_6_out);
  Button m (.out(m_out));
  xor xor_7 (xor_7_out, or_2_out, Lock);
  Button n (.out(n_out));
  Button o (.out(o_out));
  _6bitadder_main main_4 (
    .B5(xor_6_out), .A5(xor_8_out), .B4(main_2_out_13), .A4(xor_8_out), .B3(main_2_s3), .A3(xor_8_out),
    .B2(main_2_s2), .A2(xor_7_out), .B1(main_2_out_16), .A1(xor_7_out), .B0(1'b0), .in_12(main_2_s0),
    .A0(xor_8_out), .S6(main_4_s6), .S5(main_4_s5), .out_14(main_4_out_14), .S3(main_4_s3), .S2(main_4_s2),
    .out_17(main_4_out_17), .S0(main_4_s0));
  xor xor_8 (xor_8_out, 1'b0, Lock);
  Button p (.out(p_out));
  Button q (.out(q_out));
  Button r (.out(r_out));
  _5bitadder_main main_5 (
    .B4(1'b0), .A4(main_4_out_14), .B3(1'b0), .A3(main_4_s3), .B2(1'b0), .A2(main_4_s2), .B1(1'b0),
    .A1(main_4_out_17), .B0(1'b0), .in_10(Lock), .A0(main_4_s0), .out_13(main_5_out_13), .S3(main_5_s3),
    .S2(main_5_s2), .out_16(main_5_out_16), .S0(main_5_s0));  // open: out_12
  Button s (.out(s_out));
  Button t (.out(t_out));
  _7bitadder_main main_6 (
    .in_2(1'b1), .in_3(1'b0), .in_4(not_1_out), .in_5(1'b0), .in_6(1'b0), .in_7(main_5_out_13), .in_8(1'b0),
    .in_9(main_5_s3), .in_10(1'b0), .in_11(main_5_s2), .in_12(1'b0), .in_13(main_5_out_16), .in_1(1'b0),
    .in_14(1'b1), .in_15(main_5_s0), .out_17(main_6_out_23[6]), .out_18(main_6_out_23[5]),
    .out_19(main_6_out_23[4]), .out_20(main_6_out_23[3]), .out_21(main_6_out_23[2]),
    .out_22(main_6_out_23[1]), .out_23(main_6_out_23[0]));  // open: out_16
  Button u (.out(u_out));
  Button w (.out(w_out));
  Button v (.out(v_out));
  TTY tty_1 (.data(main_6_out_23), .clk(not_3_out), .clr(button_1_out));  // open: we
  Button button_1 (.out(button_1_out));
  Button x (.out(x_out));
  Button z (.out(z_out));
  Button y (.out(y_out));

  // Notes on the sheet:
  //   Encoder
  //   Shift
  //   Amount
  //   Encrypt(0)
  //   Decrypt(1)
  //   Adder
  //   /Subtractor
  //   CEASER CIPHER ENCRYPTION AND DECRYPTION
  //   16CO121-16CO202
  //   Encoder
  //   Clear
endmodule
