// Logisim project 5bitadder.circ as structural Verilog: 1 circuit, main circuit main
module main (
  input  B0,
  input  B4,
  input  A4,
  input  B3,
  input  A3,
  input  B2,
  input  A2,
  input  B1,
  input  A1,
  input  in_10,
  input  A0,
  output out_12,
  output out_13,
  output S3,
  output S2,
  output out_16,
  output S0
);

  wire main_2_carry, main_3_carry, main_4_carry, main_5_carry;

  fulladder_main main_1 (.A(A4), .B(B4), .Cin(main_2_carry), .Sum(out_13), .Carry(out_12));
  fulladder_main main_2 (.A(A3), .B(B3), .Cin(main_3_carry), .Sum(S3), .Carry(main_2_carry));
  fulladder_main main_3 (.A(A2), .B(B2), .Cin(main_4_carry), .Sum(S2), .Carry(main_3_carry));
  fulladder_main main_4 (.A(A1), .B(B1), .Cin(main_5_carry), .Sum(out_16), .Carry(main_4_carry));
  fulladder_main main_5 (.A(A0), .B(in_10), .Cin(B0), .Sum(S0), .Carry(main_5_carry));

  // Notes on the sheet:
  //   S5
  //   S4
  //   5 BIT BINARY RIPPLE ADDER
  //   S1
endmodule
