// Logisim project alpha_to_bin.circ as structural Verilog: 1 circuit, main circuit main
module main (
  input  a,
  input  b,
  input  c,
  input  d,
  input  e,
  input  f,
  input  g,
  input  h,
  input  i,
  input  j,
  input  k,
  input  l,
  input  m,
  input  n,
  input  o,
  input  p,
  input  q,
  input  r,
  input  s,
  input  t,
  input  u,
  input  v,
  input  w,
  input  x,
  input  y,
  input  z,
  output out_27,
  output out_28,
  output out_29,
  output out_30,
  output out_31
);

  wire or_1_out, or_2_out, or_4_out, or_5_out, or_6_out, or_7_out, or_8_out, or_9_out, or_10_out, or_11_out,
       or_13_out, or_14_out, or_15_out;

  or or_1 (or_1_out, q, r, s, t, u);
  or or_2 (or_2_out, v, w, x, y, z);
  or or_3 (out_27, or_1_out, or_2_out);
  or or_4 (or_4_out, i, j, k, l, m);
  or or_5 (or_5_out, n, o, p, y, z);
  or or_6 (or_6_out, c, d, g, h, k);
  or or_7 (or_7_out, l, o, p, s, t);
  or or_8 (or_8_out, w, x);
  or or_9 (or_9_out, b, h, d, f, j);
  or or_10 (or_10_out, l, n, p, r, t);
  or or_11 (or_11_out, v, x, z);
  or or_12 (out_28, or_4_out, or_5_out);
  or or_13 (or_13_out, e, f, m, g, h);
  or or_14 (or_14_out, o, n, p, u, v);
  or or_15 (or_15_out, w, x);
  or or_16 (out_29, or_13_out, or_14_out, or_15_out);
  or or_17 (out_30, or_6_out, or_7_out, or_8_out);
  or or_18 (out_31, or_9_out, or_10_out, or_11_out);

  // Notes on the sheet:
  //   choice
endmodule
