// Logisim project shift_to_bin.circ as structural Verilog: 1 circuit, main circuit main
module main (
  input  _1,
  input  _2,
  input  _3,
  input  _4,
  input  _5,
  input  _6,
  input  _7,
  input  _8,
  input  _9,
  input  _10,
  input  _11,
  input  _12,
  input  _13,
  input  _14,
  input  _15,
  input  _16,
  input  _17,
  input  _18,
  input  _19,
  input  _20,
  input  _21,
  input  _22,
  input  _23,
  input  _24,
  input  _25,
  input  _26,
  output out_27,
  output out_28,
  output out_29,
  output out_30,
  output out_31
);

  wire or_1_out, or_2_out, or_4_out, or_5_out, or_6_out, or_7_out, or_8_out, or_9_out, or_10_out, or_11_out,
       or_13_out, or_14_out, or_15_out;

  or or_1 (or_1_out, _16, _17, _18, _19, _20);
  or or_2 (or_2_out, _21, _22, _23, _24, _25);
  or or_3 (out_27, or_1_out, _26, or_2_out);
  or or_4 (or_4_out, _8, _9, _10, _11, _12);
  or or_5 (or_5_out, _13, _14, _15, _24, _25);
  or or_6 (or_6_out, _2, _3, _6, _7, _10);
  or or_7 (or_7_out, _11, _14, _15, _18, _19);
  or or_8 (or_8_out, _22, _23);
  or or_9 (or_9_out, _1, _7, _3, _5, _9);
  or or_10 (or_10_out, _11, _13, _15, _17, _19);
  or or_11 (or_11_out, _21, _23, _25);
  or or_12 (out_28, or_4_out, _26, or_5_out);
  or or_13 (or_13_out, _4, _5, _12, _6, _7);
  or or_14 (or_14_out, _14, _13, _15, _20, _21);
  or or_15 (or_15_out, _22, _23);
  or or_16 (out_29, or_13_out, or_14_out, or_15_out);
  or or_17 (out_30, or_6_out, _26, or_7_out, or_8_out);
  or or_18 (out_31, or_9_out, or_10_out, or_11_out);
endmodule
